# Fritzing sketch hydroponics (saved by Fritzing 0.9.3b)
breadboards: 1

parts:
  ESP-01 = ESP8266 WiFi Module [part_number=ESP8266]
  C1_-_100uf = Capacitor Polarized [package=cpol-radial-100uf-25v]
  R2 = Resistor [tolerance=±5% resistance=3.3k package=THT]
  IC1 = V_REG_LD1117VXX [package=78xxl]
  PhotoCell = Photocell (LDR) [package=THT]
  IC2 = IC, DIP package, 4 pins [chip_label=AMT1001]
  R3 = Resistor [tolerance=±5% resistance=10k package=THT]
  Water_Pump_Relay = KY-019 5V Relay Module [package="Breakout board"]
  LLC = Logic Level Converter
  R4 = Resistor [tolerance=±5% resistance=1k package=THT]
  WaterTemp_&_EC = DS18B20 1-Wire Temperature Sensor Probe Cable
  110v_Plug_(EC) = female pin header, 2 pins [form="♀ (female)"]
  Part1 = Arduino Nano (Rev3.0)
  YF-S201_Flow_Meter1 = YF-S201 Water Flow Meter
  Float_Sensor = Round Pushbutton
  R5 = Resistor [tolerance=±5% resistance=1k package=THT]

nets:
  N1: ESP-01.RXD, LLC.RX_LV
  N2: ESP-01.VCC, ESP-01.RST, ESP-01.CH_PD, C1_-_100uf.+, IC1.OUT, LLC.LV
  GND: ESP-01.GND, C1_-_100uf.-, R2.Pin_0, IC1.GND, IC2.pin2, R3.Pin_0, Water_Pump_Relay.-, LLC.GND, Part1.GND, YF-S201_Flow_Meter1.GND, R5.Pin_0
  N3: ESP-01.TXD, LLC.TX_LV
  N4: R2.Pin_1, PhotoCell.pin_0, Part1.A5
  5V: IC1.IN, PhotoCell.pin_1, IC2.pin1, Water_Pump_Relay.+, LLC.HV, Part1.VIN, YF-S201_Flow_Meter1.VCC, Float_Sensor.leg1
  N5: IC2.pin3, R3.Pin_1, Part1.A7
  N6: IC2.pin4, Part1.A6
  N7: Water_Pump_Relay.S, Part1.D4
  N8: LLC.TX_HV, Part1.D1/TX
  N9: LLC.RX_HV, Part1.D0/RX
  N10: R4.Pin_0, Part1.A4
  N11: R4.Pin_1, 110v_Plug_(EC).pin1, Part1.A0
  N12: WaterTemp_&_EC.GND, Part1.D8
  N13: WaterTemp_&_EC.DQ, Part1.D10
  N14: WaterTemp_&_EC.VDD, Part1.D9
  N15: 110v_Plug_(EC).pin2, Part1.A1
  N16: Part1.D3, Float_Sensor.leg0, R5.Pin_1
  N17: Part1.D5, YF-S201_Flow_Meter1.SIG

custom parts:
  ESP8266 WiFi Module: Generic WiFi Module based on the ESP8266 with onboard PCB antenna and UART communications
  KY-019 5V Relay Module: KY-019 5V Relay module, used to control AC circuits.
  YF-S201 Water Flow Meter: The YF-S201 Flow Meter. The input voltage is 5V to 24V (DC).
